// Logisim project ALU8.circ as structural Verilog: 2 circuits, main circuit main
module main (
  input  [7:0] in_1,
  input  [7:0] in_2,
  input  [2:0] OP,
  output [7:0] out_4,
  output Z,
  output LT
);

  wire [7:0] adder_1_out, adder_2_out, and_1_out, multiplexer_1_out, multiplexer_2_out, not_1_out, or_1_out,
       subtractor_1_out, subtractor_2_out, xor_1_out;

  Adder adder_1 (.a(in_1), .b(in_2), .out(adder_1_out));  // open: cin, cout
  Adder adder_2 (.a(in_1), .b(8'h1), .out(adder_2_out));  // open: cin, cout
  Subtractor subtractor_1 (.a(in_1), .b(in_2), .out(subtractor_1_out));  // open: bin, bout
  Subtractor subtractor_2 (.a(in_1), .b(8'h1), .out(subtractor_2_out));  // open: bin, bout
  assign and_1_out = in_1 & in_2;  // AND_Gate and_1, 8 bits wide
  assign or_1_out = in_1 | in_2;  // OR_Gate or_1, 8 bits wide
  assign not_1_out = ~in_1;  // NOT_Gate not_1, 8 bits wide
  assign xor_1_out = in_1 ^ in_2;  // XOR_Gate xor_1, 8 bits wide
  Multiplexer #(.select(2), .width(8), .enable("false")) multiplexer_1 (
    .in0(adder_1_out), .in1(adder_2_out), .in2(subtractor_1_out), .in3(subtractor_2_out),
    .out(multiplexer_1_out), .sel(OP[1:0]));
  Multiplexer #(.select(2), .width(8), .enable("false")) multiplexer_2 (
    .in0(and_1_out), .in1(or_1_out), .in2(not_1_out), .in3(xor_1_out), .out(multiplexer_2_out), .sel(OP[1:0]));
  Multiplexer #(.width(8), .enable("false")) multiplexer_3 (
    .in0(multiplexer_1_out), .in1(multiplexer_2_out), .out(out_4), .sel(OP[2]));
  nor nor_1 (Z, out_4[0], out_4[1], out_4[2], out_4[3], out_4[4], out_4[5], out_4[6], out_4[7]);
  LT lt_1 (.in_1(in_1[7]), .in_2(in_2[7]), .in_3(out_4[7]), .out_4(LT));

  // Notes on the sheet:
  //   A
  //   B
  //   AU
  //   LU
  //   R
endmodule

module LT (
  input  in_1,
  input  in_2,
  input  in_3,
  output out_4
);

  wire and_1_out, and_2_out, and_3_out, not_1_out;

  not not_1 (not_1_out, in_2);
  and and_1 (and_1_out, in_1, not_1_out);
  and and_2 (and_2_out, not_1_out, in_3);
  and and_3 (and_3_out, in_1, in_3);
  or or_1 (out_4, and_1_out, and_2_out, and_3_out);
endmodule
