// Logisim project TN1.circ as structural Verilog: 1 circuit, main circuit ADDSUB4
module ADDSUB4 (
  input  [3:0] A,
  input  [3:0] B,
  input  SUB,
  output [3:0] out_4,
  output [3:0] out_5
);

  wire adder_1_cout, adder_2_cout, adder_3_cout, adder_4_cout;

  xor xor_1 (out_5[0], B[0], SUB);
  xor xor_2 (out_5[1], B[1], SUB);
  xor xor_3 (out_5[2], B[2], SUB);
  xor xor_4 (out_5[3], B[3], SUB);
  Adder #(.width(1)) adder_1 (.a(A[0]), .b(B[0]), .out(out_4[0]), .cin(SUB), .cout(adder_1_cout));
  // Probe on adder_1_cout
  Adder #(.width(1)) adder_2 (.a(A[1]), .b(B[1]), .out(out_4[1]), .cin(adder_1_cout), .cout(adder_2_cout));
  // Probe on adder_2_cout
  Adder #(.width(1)) adder_3 (.a(A[2]), .b(B[2]), .out(out_4[2]), .cin(adder_2_cout), .cout(adder_3_cout));
  // Probe on adder_3_cout
  Adder #(.width(1)) adder_4 (.a(A[3]), .b(B[3]), .out(out_4[3]), .cin(adder_3_cout), .cout(adder_4_cout));
  // Probe on adder_4_cout
endmodule
