// Logisim project TN3.circ as structural Verilog
module DLATCH (
  input  E,
  input  D,
  output Q
);

  Multiplexer #(.enable("false")) multiplexer_1 (.in0(Q), .in1(D), .out(Q), .sel(E));
endmodule

module TN3 (
  input  CLK,
  input  in_2,
  output out_3,
  output out_4
);

  wire d_ff_1_q, dlatch_1_q;

  DLATCH dlatch_1 (.D(in_2), .E(CLK), .Q(dlatch_1_q));
  D_Flip_Flop d_ff_1 (.clk(CLK), .D(in_2), .Q(d_ff_1_q));  // open: Qn, preset, en, reset
  DLATCH dlatch_2 (.D(dlatch_1_q), .E(CLK), .Q(out_3));
  D_Flip_Flop d_ff_2 (.clk(CLK), .D(d_ff_1_q), .Q(out_4));  // open: Qn, preset, en, reset

  // Notes on the sheet:
  //   D
  //   DLATCH1
  //   FF1
  //   DLATCH2
  //   FF2
endmodule
