// Logisim project TN4.circ as structural Verilog: 4 circuits, main circuit DATAPATH
module REGFILE (
  input  WE,
  input  [1:0] RA,
  input  [1:0] RD,
  input  [1:0] RB,
  input  [7:0] DIN,
  input  CLK,
  output [7:0] R0,
  output [7:0] QA,
  output [7:0] R1,
  output [7:0] QB,
  output [7:0] R2,
  output [7:0] R3
);

  wire decoder_1_out0, decoder_1_out1, decoder_1_out2, decoder_1_out3;

  Decoder #(.select(2)) decoder_1 (
    .out0(decoder_1_out0), .out1(decoder_1_out1), .out2(decoder_1_out2), .out3(decoder_1_out3), .sel(RD),
    .en(WE));
  Register u_R0 (.D(DIN), .en(decoder_1_out0), .Q(R0), .clk(CLK));  // open: clr
  Register u_R1 (.D(DIN), .en(decoder_1_out1), .Q(R1), .clk(CLK));  // open: clr
  Register u_R2 (.D(DIN), .en(decoder_1_out2), .Q(R2), .clk(CLK));  // open: clr
  Register u_R3 (.D(DIN), .en(decoder_1_out3), .Q(R3), .clk(CLK));  // open: clr
  Multiplexer #(.select(2), .width(8)) multiplexer_1 (
    .in0(R0), .in1(R1), .in2(R2), .in3(R3), .out(QA), .sel(RA));  // open: en
  Multiplexer #(.select(2), .width(8)) multiplexer_2 (
    .in0(R0), .in1(R1), .in2(R2), .in3(R3), .out(QB), .sel(RB));  // open: en
endmodule

module DATAPATH (
  input  WE,
  input  [1:0] RD,
  input  [2:0] OP,
  input  [1:0] RA,
  input  [7:0] IMM,
  input  [1:0] RB,
  input  CLK,
  input  SRC,
  output [7:0] R0,
  output [7:0] R1,
  output z,
  output [7:0] R2,
  output [7:0] R3
);

  wire [7:0] alu8_1_r, multiplexer_1_out, regfile_1_qa, regfile_1_qb;

  REGFILE regfile_1 (
    .WE(WE), .RD(RD), .DIN(multiplexer_1_out), .CLK(CLK), .RA(RA), .RB(RB), .R0(R0), .QA(regfile_1_qa),
    .R1(R1), .QB(regfile_1_qb), .R2(R2), .R3(R3));
  ALU8 alu8_1 (.A(regfile_1_qa), .B(regfile_1_qb), .OP(OP), .R(alu8_1_r), .Z(z));  // open: LT
  Multiplexer #(.width(8), .enable("false")) multiplexer_1 (
    .in0(alu8_1_r), .in1(IMM), .out(multiplexer_1_out), .sel(SRC));
endmodule

module ALU8 (
  input  [7:0] A,
  input  [7:0] B,
  input  [2:0] OP,
  output [7:0] R,
  output Z,
  output LT
);

  wire [7:0] adder_1_out, adder_2_out, and_1_out, multiplexer_1_out, multiplexer_2_out, not_1_out, or_1_out,
       subtractor_1_out, subtractor_2_out, xor_1_out;

  Adder adder_1 (.a(A), .b(B), .out(adder_1_out));  // open: cin, cout
  Adder adder_2 (.a(A), .b(8'h1), .out(adder_2_out));  // open: cin, cout
  Subtractor subtractor_1 (.a(A), .b(B), .out(subtractor_1_out));  // open: bin, bout
  Subtractor subtractor_2 (.a(A), .b(8'h1), .out(subtractor_2_out));  // open: bin, bout
  assign and_1_out = A & B;  // AND_Gate and_1, 8 bits wide
  assign or_1_out = A | B;  // OR_Gate or_1, 8 bits wide
  assign not_1_out = ~A;  // NOT_Gate not_1, 8 bits wide
  assign xor_1_out = A ^ B;  // XOR_Gate xor_1, 8 bits wide
  Multiplexer #(.select(2), .width(8), .enable("false")) multiplexer_1 (
    .in0(adder_1_out), .in1(adder_2_out), .in2(subtractor_1_out), .in3(subtractor_2_out),
    .out(multiplexer_1_out), .sel(OP[1:0]));
  Multiplexer #(.select(2), .width(8), .enable("false")) multiplexer_2 (
    .in0(and_1_out), .in1(or_1_out), .in2(not_1_out), .in3(xor_1_out), .out(multiplexer_2_out), .sel(OP[1:0]));
  Multiplexer #(.width(8), .enable("false")) multiplexer_3 (
    .in0(multiplexer_1_out), .in1(multiplexer_2_out), .out(R), .sel(OP[2]));
  nor nor_1 (Z, R[0], R[1], R[2], R[3], R[4], R[5], R[6], R[7]);
  LT lt_1 (.in_1(A[7]), .in_2(B[7]), .in_3(R[7]), .out_4(LT));

  // Notes on the sheet:
  //   AU
  //   LU
endmodule

module LT (
  input  in_1,
  input  in_2,
  input  in_3,
  output out_4
);

  wire and_1_out, and_2_out, and_3_out, not_1_out;

  not not_1 (not_1_out, in_2);
  and and_1 (and_1_out, in_1, not_1_out);
  and and_2 (and_2_out, not_1_out, in_3);
  and and_3 (and_3_out, in_1, in_3);
  or or_1 (out_4, and_1_out, and_2_out, and_3_out);
endmodule
